# Fritzing sketch heart_project (saved by Fritzing 1.0.4)
breadboards: 1

parts:
  Bauteil1 = Arduino Uno (Rev3) - ICSP
  U1 = LCD-16X2 [package=lcd-16x2]
  R1 = Rotary Potentiometer (Small) [maximum_resistance=10kΩ knob_status=50% power=0.5W package=THT]
  R2 = Resistor [tolerance=±5% power=0.25W resistance=220 package=THT]
  Next = Pushbutton [package="[THT]"]
  Back = Pushbutton [package="[THT]"]
  Select = Pushbutton [package="[THT]"]
  Previous = Pushbutton [package="[THT]"]

nets:
  N1: Bauteil1.ICSP_MISO, Bauteil1.D12/MISO, U1.RS
  5V: Bauteil1.5V, U1.VDD, R1.leg1, R2.Pin_1
  N2: Bauteil1.D8, Next.Pin_3, Next.Pin_4
  N3: Bauteil1.D9_PWM, Previous.Pin_3, Previous.Pin_4
  N4: Bauteil1.D11_PWM/MOSI, U1.E
  N5: Bauteil1.D2, U1.DB7
  N6: Bauteil1.D3_PWM, U1.DB6
  N7: Bauteil1.D4, U1.DB5
  N8: Bauteil1.D5_PWM, U1.DB4
  N9: Bauteil1.D6_PWM, Back.Pin_3, Back.Pin_4
  N10: Bauteil1.D7, Select.Pin_3, Select.Pin_4
  GND: Bauteil1.GND, U1.VSS, U1.R_W, U1.K, R1.leg2, Next.Pin_1, Next.Pin_2, Back.Pin_1, Back.Pin_2, Select.Pin_1, Select.Pin_2, Previous.Pin_1, Previous.Pin_2
  N11: U1.VO, R1.wiper
  N12: U1.A, R2.Pin_0
